# Fritzing sketch Pollution Monitor Sketch (saved by Fritzing 0.9.3b)
breadboards: 2

parts:
  Part1 = DHT22 module
  U1 = Sharp Dust Sensor [part_number=GP2Y1010AU0F]
  U2 = LM2596 step down module
  F1 = Fan - Ventilador [package=THT]
  VCC1 = 4 x AAA Battery Mount  # not connected
  esp1 = ESP32 DevKitc V4
  R1 = Resistor [tolerance=±5% resistance=150 package="0402 [SMD]"]
  C3 = Electrolytic Capacitor [capacitance=0.22mF package="0405 [SMD, electrolytic]"]
  R2 = Resistor [tolerance=±5% resistance=6.8k package="0402 [SMD]"]
  R3 = Resistor [tolerance=±5% resistance=10k package="0402 [SMD]"]
  Mod1 = L298N DC motor driver
  VCC2 = Battery block 9V
  Part2 = MQ-7 breakout
  Part3 = DHT22 module
  Part4 = DHT22 module
  Part5 = MQ-7 breakout
  R6 = Resistor [tolerance=±5% resistance=6.8k package="0402 [SMD]"]
  Part6 = MQ-7 breakout
  A1 = DFR Sen0575
  R7 = Resistor [tolerance=±5% resistance=6.8k package="0402 [SMD]"]
  R8 = Resistor [tolerance=±5% resistance=10k package="0402 [SMD]"]
  R9 = Resistor [tolerance=±5% resistance=10k package="0402 [SMD]"]
  R11 = Resistor [tolerance=±5% resistance=10k package="0402 [SMD]"]
  R12 = Resistor [tolerance=±5% resistance=6.8k package="0805 [SMD]"]
  LED1 = LED - 5mm [color="Red (633nm)" package="5 mm [THT]"]
  LED2 = LED - 5mm [color="White (4500K)" package="5 mm [THT]"]
  LED3 = LED - 5mm [color="Yellow (595nm)" package="5 mm [THT]"]
  LED4 = LED - 5mm [color="Green (555nm)" package="5 mm [THT]"]
  R13 = Resistor [tolerance=±5% resistance=220 package="0402 [SMD]"]
  R14 = Resistor [tolerance=±5% resistance=220 package="0402 [SMD]"]
  R15 = Resistor [tolerance=±5% resistance=220 package="0402 [SMD]"]
  R16 = Resistor [tolerance=±5% resistance=220 package="0402 [SMD]"]

nets:
  N1: Part1.VCC, esp1.IO21
  GND: Part1.GND, U1.LED-GND, U1.S-GND, U2.IN-, U2.OUT-, esp1.GND, C3.-, R3.Pin_1, Part2.GND, Part3.GND, Part4.GND, Part5.GND, Part6.GND, A1.Pin_4, R8.Pin_1, R9.Pin_1, R11.Pin_0
  VCC: Part1.DATA, esp1.3V3, Part2.VCC, Part3.DATA, Part4.DATA, Part5.VCC, Part6.VCC, A1.Pin_3
  N2: U1.V-LED, R1.Pin_0, C3.+
  N3: U1.LED, esp1.IO5
  N4: U1.VCC, U2.OUT+
  N5: F1.5V, Mod1.OUT1
  N6: F1.GND, Mod1.OUT2
  N7: esp1.IO16, LED1.anode
  N8: esp1.IO17, LED3.anode
  N9: esp1.IO18, LED2.anode
  N10: esp1.IO19, LED4.anode
  N11: esp1.IO22, Part4.VCC
  N12: esp1.IO23, Part3.VCC
  N13: esp1.VP, R7.Pin_1, R8.Pin_0
  N14: esp1.VN, R2.Pin_1, R3.Pin_0
  N15: esp1.IO32, R6.Pin_1, R9.Pin_0
  N16: esp1.IO33, R11.Pin_1, R12.Pin_0
  N17: esp1.IO25, A1.Pin_1
  N18: esp1.IO27, Mod1.ENA
  N19: esp1.IO14, Mod1.IN1
  N20: R2.Pin_0, Part5.AO
  N21: Mod1.12V, Mod1.5V-ENA-JMP-O, VCC2.+
  N22: Mod1.GND, VCC2.-
  N23: Part2.AO, R6.Pin_0
  N24: Part6.AO, R12.Pin_1
  N25: LED1.cathode, R13.Pin_1
  N26: LED2.cathode, R15.Pin_1
  N27: LED3.cathode, R16.Pin_1
  N28: LED4.cathode, R14.Pin_1

notes:
  12 V
  MEMS NO2 DFRobot Sensor

custom parts:
  Sharp Dust Sensor: Sharp GP2Y1010AU0F Dust Sensor
  LM2596 step down module: LM2596 DC-DC step down power supply module 3 A.
  Fan - Ventilador: Ventilador de 2 pines, se encuentra comunmente en computadoras de escritorio
  ESP32 DevKitc V4: ESP32-DevKitC board with ESP32-WROOM-32 module. ESP32-DevKitC V4 is a small-sized ESP32-based development board produced by Espressif. Most of the pins on the ESP module are broken out to the pin headers on the board. The pins D0, D1, D2, D3, CMD and CLK are used internally for communication between ESP32 and SPI flash memory. They are grouped on both sides near the USB connector. Avoid using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
  L298N DC motor driver: 2x DC motor driver with 78M05 positive voltage regulator (7..35 V) L298N: max 46 V, 2 A Set 5 V Enable jumper to enable 5 V regultor (needed for the L298N) and +5 V output at screw terminal or supply external +5 V at screw terminal Set ENA and/or ENB to +5 V to enable motor permanently or supply ENA and/or ENB with PWM signal IN1 and IN2 set rotation directory for motor A (OUT1/OUT2) IN2 and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
  MQ-7 breakout: SKU: 101282
  DFR Sen0575: Based on the principle of tipping bucket rainfall, the rainfall sensor provides users with rainfall values in millimeters and system operating time.
